// Logisim project project_8x8.circ as structural Verilog: 5 circuits, main circuit main
module main (
);

  wire button_1_out, button_2_out, clock_1_out, not_1_out;
  wire [2:0] counter_1_q;
  wire [6:0] bitselector_2_out, keyboard_1_data;
  wire [7:0] bitselector_1_out, ram_1_dout;

  Counter #(.max('h7), .width(3)) counter_1 (
    .Q(counter_1_q), .clk(clock_1_out), .clr(button_1_out));  // open: load, D, count, carry, up
  Button button_1 (.out(button_1_out));
  Keyboard keyboard_1 (.clk(clock_1_out), .data(keyboard_1_data));  // open: re, clr, avail
  Clock clock_1 (.out(clock_1_out));
  BitSelector #(.group(8), .width(7)) bitselector_1 (.in(keyboard_1_data), .out(bitselector_1_out), .sel(clock_1_out));
  not not_1 (not_1_out, clock_1_out);
  RAM #(.addrWidth(3)) ram_1 (
    .addr(counter_1_q), .we(clock_1_out), .oe(not_1_out), .clk(clock_1_out), .din(bitselector_1_out),
    .dout(ram_1_dout));
  BitSelector #(.group(7)) bitselector_2 (.in(ram_1_dout), .out(bitselector_2_out), .sel(clock_1_out));
  TTY #(.rows(16)) tty_1 (.data(bitselector_2_out), .clk(clock_1_out), .we(1'b1), .clr(button_2_out));
  Button button_2 (.out(button_2_out));
endmodule

module RAM_4X4 (
  input  [3:0] Data_input,
  input  [1:0] Address,
  input  RD,
  input  CS,
  input  OE,
  output [3:0] Data_output
);

  wire and_1_out, and_2_out, and_3_out, and_4_out, and_5_out, and_6_out, and_7_out, and_8_out, and_9_out,
       and_10_out, and_11_out, and_12_out, and_13_out, and_14_out, and_15_out, and_16_out, and_17_out,
       and_18_out, and_19_out, and_20_out, and_21_out, and_22_out, and_23_out, and_24_out, and_25_out,
       and_26_out, d_ff_1_q, d_ff_2_q, d_ff_3_q, d_ff_4_q, d_ff_5_q, d_ff_6_q, d_ff_7_q, d_ff_8_q, d_ff_9_q,
       d_ff_10_q, d_ff_11_q, d_ff_12_q, d_ff_13_q, d_ff_14_q, d_ff_15_q, d_ff_16_q, not_1_out, not_2_out,
       not_3_out, or_1_out, or_2_out, or_3_out, or_4_out;

  not not_1 (not_1_out, Address[0]);
  not not_2 (not_2_out, Address[1]);
  and and_1 (and_1_out, not_1_out, not_2_out);
  and and_2 (and_2_out, Address[0], not_2_out);
  and and_3 (and_3_out, not_1_out, Address[1]);
  and and_4 (and_4_out, Address[0], Address[1]);
  and and_5 (and_5_out, CS, RD);
  D_Flip_Flop d_ff_1 (.D(Data_input[0]), .clk(and_6_out), .Q(d_ff_1_q));  // open: Qn, preset, reset
  and and_6 (and_6_out, and_5_out, and_1_out);
  D_Flip_Flop d_ff_2 (.D(Data_input[0]), .clk(and_7_out), .Q(d_ff_2_q));  // open: Qn, preset, reset
  and and_7 (and_7_out, and_5_out, and_2_out);
  D_Flip_Flop d_ff_3 (.D(Data_input[0]), .clk(and_8_out), .Q(d_ff_3_q));  // open: Qn, preset, reset
  and and_8 (and_8_out, and_5_out, and_3_out);
  D_Flip_Flop d_ff_4 (.D(Data_input[0]), .clk(and_9_out), .Q(d_ff_4_q));  // open: Qn, preset, reset
  and and_9 (and_9_out, and_5_out, and_4_out);
  not not_3 (not_3_out, RD);
  and and_10 (and_10_out, not_3_out, CS, OE);
  and and_11 (and_11_out, and_3_out, d_ff_3_q);
  and and_12 (and_12_out, and_4_out, d_ff_4_q);
  D_Flip_Flop d_ff_5 (.D(Data_input[1]), .clk(and_6_out), .Q(d_ff_5_q));  // open: Qn, preset, reset
  and and_13 (and_13_out, and_1_out, d_ff_1_q);
  D_Flip_Flop d_ff_6 (.D(Data_input[1]), .clk(and_7_out), .Q(d_ff_6_q));  // open: Qn, preset, reset
  and and_14 (and_14_out, and_2_out, d_ff_2_q);
  D_Flip_Flop d_ff_7 (.D(Data_input[1]), .clk(and_8_out), .Q(d_ff_7_q));  // open: Qn, preset, reset
  D_Flip_Flop d_ff_8 (.D(Data_input[1]), .clk(and_9_out), .Q(d_ff_8_q));  // open: Qn, preset, reset
  or or_1 (or_1_out, and_12_out, and_11_out, and_14_out, and_13_out);
  assign Data_output[0] = and_10_out ? or_1_out : 1'bz;  // Controlled_Buffer controlled_buffer_1
  and and_15 (and_15_out, and_4_out, d_ff_8_q);
  and and_16 (and_16_out, and_1_out, d_ff_5_q);
  and and_17 (and_17_out, and_2_out, d_ff_6_q);
  and and_18 (and_18_out, and_3_out, d_ff_7_q);
  or or_2 (or_2_out, and_15_out, and_18_out, and_17_out, and_16_out);
  assign Data_output[1] = and_10_out ? or_2_out : 1'bz;  // Controlled_Buffer controlled_buffer_2
  D_Flip_Flop d_ff_9 (.D(Data_input[2]), .clk(and_6_out), .Q(d_ff_9_q));  // open: Qn, preset, reset
  D_Flip_Flop d_ff_10 (.D(Data_input[2]), .clk(and_7_out), .Q(d_ff_10_q));  // open: Qn, preset, reset
  D_Flip_Flop d_ff_11 (.D(Data_input[2]), .clk(and_8_out), .Q(d_ff_11_q));  // open: Qn, preset, reset
  D_Flip_Flop d_ff_12 (.D(Data_input[2]), .clk(and_9_out), .Q(d_ff_12_q));  // open: Qn, preset, reset
  and and_19 (and_19_out, and_4_out, d_ff_12_q);
  and and_20 (and_20_out, and_1_out, d_ff_9_q);
  and and_21 (and_21_out, and_2_out, d_ff_10_q);
  and and_22 (and_22_out, and_3_out, d_ff_11_q);
  or or_3 (or_3_out, and_19_out, and_22_out, and_21_out, and_20_out);
  assign Data_output[2] = and_10_out ? or_3_out : 1'bz;  // Controlled_Buffer controlled_buffer_3
  D_Flip_Flop d_ff_13 (.D(Data_input[3]), .clk(and_6_out), .Q(d_ff_13_q));  // open: Qn, preset, reset
  D_Flip_Flop d_ff_14 (.D(Data_input[3]), .clk(and_7_out), .Q(d_ff_14_q));  // open: Qn, preset, reset
  D_Flip_Flop d_ff_15 (.D(Data_input[3]), .clk(and_8_out), .Q(d_ff_15_q));  // open: Qn, preset, reset
  D_Flip_Flop d_ff_16 (.D(Data_input[3]), .clk(and_9_out), .Q(d_ff_16_q));  // open: Qn, preset, reset
  and and_23 (and_23_out, and_1_out, d_ff_13_q);
  and and_24 (and_24_out, and_2_out, d_ff_14_q);
  and and_25 (and_25_out, and_3_out, d_ff_15_q);
  and and_26 (and_26_out, and_4_out, d_ff_16_q);
  or or_4 (or_4_out, and_26_out, and_25_out, and_24_out, and_23_out);
  assign Data_output[3] = and_10_out ? or_4_out : 1'bz;  // Controlled_Buffer controlled_buffer_4
endmodule

module with_RAM4X4 (
  input  [1:0] A0_A1,
  input  RD,
  input  A2,
  input  OE,
  input  [7:0] Data_input,
  output [7:0] out_6
);

  wire not_1_out, not_2_out;
  wire [7:0] RAM1_data_output, RAM3_data_output;

  not not_1 (not_1_out, A2);
  RAM_4X4 RAM1 (
    .Data_input(Data_input[3:0]), .Address(A0_A1), .RD(RD), .CS(not_1_out), .OE(OE),
    .Data_output(RAM1_data_output[3:0]));
  RAM_4X4 RAM3 (
    .Data_input(Data_input[3:0]), .Address(A0_A1), .RD(RD), .CS(A2), .OE(OE),
    .Data_output(RAM3_data_output[3:0]));
  not not_2 (not_2_out, A2);
  RAM_4X4 RAM2 (
    .Data_input(Data_input[7:4]), .Address(A0_A1), .RD(RD), .CS(not_2_out), .OE(OE),
    .Data_output(RAM1_data_output[7:4]));
  RAM_4X4 RAM4 (
    .Data_input(Data_input[7:4]), .Address(A0_A1), .RD(RD), .CS(A2), .OE(OE),
    .Data_output(RAM3_data_output[7:4]));
  Multiplexer #(.width(8)) multiplexer_1 (.in0(RAM1_data_output), .in1(RAM3_data_output), .out(out_6), .sel(A2));
endmodule

module RAM_8X8 (
  input  [7:0] Data_input,
  input  [2:0] Address,
  input  RD,
  input  CS,
  input  OE,
  output [7:0] Data_output
);

  wire and_1_out, and_2_out, and_3_out, and_4_out, and_5_out, and_6_out, and_7_out, and_8_out, and_9_out,
       and_10_out, and_11_out, and_12_out, and_13_out, and_14_out, and_15_out, and_16_out, and_17_out,
       and_18_out, and_19_out, and_20_out, and_21_out, and_22_out, and_23_out, and_24_out, and_25_out,
       and_26_out, and_27_out, and_28_out, and_29_out, and_30_out, and_31_out, and_32_out, and_33_out,
       and_34_out, and_35_out, and_36_out, and_37_out, and_38_out, and_39_out, and_40_out, and_41_out,
       and_42_out, and_43_out, and_44_out, and_45_out, and_46_out, and_47_out, and_48_out, and_49_out,
       and_50_out, and_51_out, and_52_out, and_53_out, and_54_out, and_55_out, and_56_out, and_57_out,
       and_58_out, and_59_out, and_60_out, and_61_out, and_62_out, and_63_out, and_64_out, and_65_out,
       and_66_out, and_67_out, and_68_out, and_69_out, and_70_out, and_71_out, and_72_out, and_73_out,
       and_74_out, and_75_out, and_76_out, and_77_out, and_78_out, and_79_out, and_80_out, and_81_out,
       and_82_out, d_ff_1_q, d_ff_2_q, d_ff_3_q, d_ff_4_q, d_ff_5_q, d_ff_6_q, d_ff_7_q, d_ff_8_q, d_ff_9_q,
       d_ff_10_q, d_ff_11_q, d_ff_12_q, d_ff_13_q, d_ff_14_q, d_ff_15_q, d_ff_16_q, d_ff_17_q, d_ff_18_q,
       d_ff_19_q, d_ff_20_q, d_ff_21_q, d_ff_22_q, d_ff_23_q, d_ff_24_q, d_ff_25_q, d_ff_26_q, d_ff_27_q,
       d_ff_28_q, d_ff_29_q, d_ff_30_q, d_ff_31_q, d_ff_32_q, d_ff_33_q, d_ff_34_q, d_ff_35_q, d_ff_36_q,
       d_ff_37_q, d_ff_38_q, d_ff_39_q, d_ff_40_q, d_ff_41_q, d_ff_42_q, d_ff_43_q, d_ff_44_q, d_ff_45_q,
       d_ff_46_q, d_ff_47_q, d_ff_48_q, d_ff_49_q, d_ff_50_q, d_ff_51_q, d_ff_52_q, d_ff_53_q, d_ff_54_q,
       d_ff_55_q, d_ff_56_q, d_ff_57_q, d_ff_58_q, d_ff_59_q, d_ff_60_q, d_ff_61_q, d_ff_62_q, d_ff_63_q,
       d_ff_64_q, not_1_out, not_2_out, not_3_out, not_4_out, or_1_out, or_2_out, or_3_out, or_4_out,
       or_5_out, or_6_out, or_7_out, or_8_out;

  not not_1 (not_1_out, Address[0]);
  not not_2 (not_2_out, Address[1]);
  not not_3 (not_3_out, Address[2]);
  and and_1 (and_1_out, not_1_out, not_2_out, not_3_out);
  and and_2 (and_2_out, Address[0], not_2_out, not_3_out);
  and and_3 (and_3_out, not_1_out, Address[1], not_3_out);
  and and_4 (and_4_out, Address[0], Address[1], not_3_out);
  and and_5 (and_5_out, not_1_out, not_2_out, Address[2]);
  and and_6 (and_6_out, Address[0], not_2_out, Address[2]);
  and and_7 (and_7_out, not_1_out, Address[1], Address[2]);
  and and_8 (and_8_out, Address[0], Address[1], Address[2]);
  and and_9 (and_9_out, and_17_out, and_1_out);
  and and_10 (and_10_out, and_17_out, and_2_out);
  and and_11 (and_11_out, and_17_out, and_3_out);
  and and_12 (and_12_out, and_17_out, and_4_out);
  and and_13 (and_13_out, and_17_out, and_5_out);
  and and_14 (and_14_out, and_17_out, and_6_out);
  and and_15 (and_15_out, and_17_out, and_7_out);
  and and_16 (and_16_out, and_17_out, and_8_out);
  and and_17 (and_17_out, CS, RD);
  not not_4 (not_4_out, RD);
  D_Flip_Flop d_ff_1 (.D(Data_input[0]), .clk(and_9_out), .Q(d_ff_1_q));  // open: Qn, preset, reset
  D_Flip_Flop d_ff_2 (.D(Data_input[0]), .clk(and_10_out), .Q(d_ff_2_q));  // open: Qn, preset, reset
  D_Flip_Flop d_ff_3 (.D(Data_input[0]), .clk(and_11_out), .Q(d_ff_3_q));  // open: Qn, preset, reset
  D_Flip_Flop d_ff_4 (.D(Data_input[0]), .clk(and_12_out), .Q(d_ff_4_q));  // open: Qn, preset, reset
  D_Flip_Flop d_ff_5 (.D(Data_input[0]), .clk(and_13_out), .Q(d_ff_5_q));  // open: Qn, preset, reset
  D_Flip_Flop d_ff_6 (.D(Data_input[0]), .clk(and_14_out), .Q(d_ff_6_q));  // open: Qn, preset, reset
  D_Flip_Flop d_ff_7 (.D(Data_input[0]), .clk(and_15_out), .Q(d_ff_7_q));  // open: Qn, preset, reset
  D_Flip_Flop d_ff_8 (.D(Data_input[0]), .clk(and_16_out), .Q(d_ff_8_q));  // open: Qn, preset, reset
  and and_18 (and_18_out, not_4_out, CS, OE);
  and and_19 (and_19_out, and_5_out, d_ff_5_q);
  and and_20 (and_20_out, and_6_out, d_ff_6_q);
  and and_21 (and_21_out, and_7_out, d_ff_7_q);
  and and_22 (and_22_out, and_8_out, d_ff_8_q);
  and and_23 (and_23_out, and_1_out, d_ff_1_q);
  and and_24 (and_24_out, and_2_out, d_ff_2_q);
  and and_25 (and_25_out, and_3_out, d_ff_3_q);
  and and_26 (and_26_out, and_4_out, d_ff_4_q);
  or or_1 (or_1_out, and_22_out, and_21_out, and_20_out, and_19_out, and_26_out, and_25_out, and_24_out, and_23_out);
  assign Data_output[0] = and_18_out ? or_1_out : 1'bz;  // Controlled_Buffer controlled_buffer_1
  D_Flip_Flop d_ff_9 (.D(Data_input[1]), .clk(and_9_out), .Q(d_ff_9_q));  // open: Qn, preset, reset
  D_Flip_Flop d_ff_10 (.D(Data_input[1]), .clk(and_10_out), .Q(d_ff_10_q));  // open: Qn, preset, reset
  D_Flip_Flop d_ff_11 (.D(Data_input[1]), .clk(and_11_out), .Q(d_ff_11_q));  // open: Qn, preset, reset
  D_Flip_Flop d_ff_12 (.D(Data_input[1]), .clk(and_12_out), .Q(d_ff_12_q));  // open: Qn, preset, reset
  D_Flip_Flop d_ff_13 (.D(Data_input[1]), .clk(and_13_out), .Q(d_ff_13_q));  // open: Qn, preset, reset
  D_Flip_Flop d_ff_14 (.D(Data_input[1]), .clk(and_14_out), .Q(d_ff_14_q));  // open: Qn, preset, reset
  D_Flip_Flop d_ff_15 (.D(Data_input[1]), .clk(and_15_out), .Q(d_ff_15_q));  // open: Qn, preset, reset
  D_Flip_Flop d_ff_16 (.D(Data_input[1]), .clk(and_16_out), .Q(d_ff_16_q));  // open: Qn, preset, reset
  and and_27 (and_27_out, and_7_out, d_ff_15_q);
  and and_28 (and_28_out, and_8_out, d_ff_16_q);
  and and_29 (and_29_out, and_3_out, d_ff_11_q);
  and and_30 (and_30_out, and_4_out, d_ff_12_q);
  and and_31 (and_31_out, and_5_out, d_ff_13_q);
  and and_32 (and_32_out, and_6_out, d_ff_14_q);
  or or_2 (or_2_out, and_28_out, and_27_out, and_32_out, and_31_out, and_30_out, and_29_out, and_34_out, and_33_out);
  D_Flip_Flop d_ff_17 (.D(Data_input[2]), .clk(and_9_out), .Q(d_ff_17_q));  // open: Qn, preset, reset
  and and_33 (and_33_out, and_1_out, d_ff_9_q);
  D_Flip_Flop d_ff_18 (.D(Data_input[2]), .clk(and_10_out), .Q(d_ff_18_q));  // open: Qn, preset, reset
  and and_34 (and_34_out, and_2_out, d_ff_10_q);
  D_Flip_Flop d_ff_19 (.D(Data_input[2]), .clk(and_11_out), .Q(d_ff_19_q));  // open: Qn, preset, reset
  D_Flip_Flop d_ff_20 (.D(Data_input[2]), .clk(and_12_out), .Q(d_ff_20_q));  // open: Qn, preset, reset
  D_Flip_Flop d_ff_21 (.D(Data_input[2]), .clk(and_13_out), .Q(d_ff_21_q));  // open: Qn, preset, reset
  D_Flip_Flop d_ff_22 (.D(Data_input[2]), .clk(and_14_out), .Q(d_ff_22_q));  // open: Qn, preset, reset
  D_Flip_Flop d_ff_23 (.D(Data_input[2]), .clk(and_15_out), .Q(d_ff_23_q));  // open: Qn, preset, reset
  D_Flip_Flop d_ff_24 (.D(Data_input[2]), .clk(and_16_out), .Q(d_ff_24_q));  // open: Qn, preset, reset
  assign Data_output[1] = and_18_out ? or_2_out : 1'bz;  // Controlled_Buffer controlled_buffer_2
  and and_35 (and_35_out, and_8_out, d_ff_24_q);
  and and_36 (and_36_out, and_4_out, d_ff_20_q);
  and and_37 (and_37_out, and_5_out, d_ff_21_q);
  and and_38 (and_38_out, and_6_out, d_ff_22_q);
  and and_39 (and_39_out, and_7_out, d_ff_23_q);
  or or_3 (or_3_out, and_35_out, and_39_out, and_38_out, and_37_out, and_36_out, and_42_out, and_41_out, and_40_out);
  and and_40 (and_40_out, and_1_out, d_ff_17_q);
  and and_41 (and_41_out, and_2_out, d_ff_18_q);
  and and_42 (and_42_out, and_3_out, d_ff_19_q);
  assign Data_output[2] = and_18_out ? or_3_out : 1'bz;  // Controlled_Buffer controlled_buffer_3
  D_Flip_Flop d_ff_25 (.D(Data_input[3]), .clk(and_9_out), .Q(d_ff_25_q));  // open: Qn, preset, reset
  D_Flip_Flop d_ff_26 (.D(Data_input[3]), .clk(and_10_out), .Q(d_ff_26_q));  // open: Qn, preset, reset
  D_Flip_Flop d_ff_27 (.D(Data_input[3]), .clk(and_11_out), .Q(d_ff_27_q));  // open: Qn, preset, reset
  D_Flip_Flop d_ff_28 (.D(Data_input[3]), .clk(and_12_out), .Q(d_ff_28_q));  // open: Qn, preset, reset
  D_Flip_Flop d_ff_29 (.D(Data_input[3]), .clk(and_13_out), .Q(d_ff_29_q));  // open: Qn, preset, reset
  D_Flip_Flop d_ff_30 (.D(Data_input[3]), .clk(and_14_out), .Q(d_ff_30_q));  // open: Qn, preset, reset
  D_Flip_Flop d_ff_31 (.D(Data_input[3]), .clk(and_15_out), .Q(d_ff_31_q));  // open: Qn, preset, reset
  D_Flip_Flop d_ff_32 (.D(Data_input[3]), .clk(and_16_out), .Q(d_ff_32_q));  // open: Qn, preset, reset
  and and_43 (and_43_out, and_5_out, d_ff_29_q);
  and and_44 (and_44_out, and_6_out, d_ff_30_q);
  and and_45 (and_45_out, and_7_out, d_ff_31_q);
  and and_46 (and_46_out, and_8_out, d_ff_32_q);
  and and_47 (and_47_out, and_1_out, d_ff_25_q);
  and and_48 (and_48_out, and_2_out, d_ff_26_q);
  and and_49 (and_49_out, and_3_out, d_ff_27_q);
  and and_50 (and_50_out, and_4_out, d_ff_28_q);
  or or_4 (or_4_out, and_46_out, and_45_out, and_44_out, and_43_out, and_50_out, and_49_out, and_48_out, and_47_out);
  assign Data_output[3] = and_18_out ? or_4_out : 1'bz;  // Controlled_Buffer controlled_buffer_4
  D_Flip_Flop d_ff_33 (.D(Data_input[4]), .clk(and_9_out), .Q(d_ff_33_q));  // open: Qn, preset, reset
  D_Flip_Flop d_ff_34 (.D(Data_input[4]), .clk(and_10_out), .Q(d_ff_34_q));  // open: Qn, preset, reset
  D_Flip_Flop d_ff_35 (.D(Data_input[4]), .clk(and_11_out), .Q(d_ff_35_q));  // open: Qn, preset, reset
  D_Flip_Flop d_ff_36 (.D(Data_input[4]), .clk(and_12_out), .Q(d_ff_36_q));  // open: Qn, preset, reset
  D_Flip_Flop d_ff_37 (.D(Data_input[4]), .clk(and_13_out), .Q(d_ff_37_q));  // open: Qn, preset, reset
  D_Flip_Flop d_ff_38 (.D(Data_input[4]), .clk(and_14_out), .Q(d_ff_38_q));  // open: Qn, preset, reset
  D_Flip_Flop d_ff_39 (.D(Data_input[4]), .clk(and_15_out), .Q(d_ff_39_q));  // open: Qn, preset, reset
  D_Flip_Flop d_ff_40 (.D(Data_input[4]), .clk(and_16_out), .Q(d_ff_40_q));  // open: Qn, preset, reset
  and and_51 (and_51_out, and_7_out, d_ff_39_q);
  and and_52 (and_52_out, and_8_out, d_ff_40_q);
  and and_53 (and_53_out, and_3_out, d_ff_35_q);
  and and_54 (and_54_out, and_4_out, d_ff_36_q);
  and and_55 (and_55_out, and_5_out, d_ff_37_q);
  and and_56 (and_56_out, and_6_out, d_ff_38_q);
  or or_5 (or_5_out, and_52_out, and_51_out, and_56_out, and_55_out, and_54_out, and_53_out, and_58_out, and_57_out);
  and and_57 (and_57_out, and_1_out, d_ff_33_q);
  and and_58 (and_58_out, and_2_out, d_ff_34_q);
  assign Data_output[4] = and_18_out ? or_5_out : 1'bz;  // Controlled_Buffer controlled_buffer_5
  D_Flip_Flop d_ff_41 (.D(Data_input[5]), .clk(and_9_out), .Q(d_ff_41_q));  // open: Qn, preset, reset
  D_Flip_Flop d_ff_42 (.D(Data_input[5]), .clk(and_10_out), .Q(d_ff_42_q));  // open: Qn, preset, reset
  D_Flip_Flop d_ff_43 (.D(Data_input[5]), .clk(and_11_out), .Q(d_ff_43_q));  // open: Qn, preset, reset
  D_Flip_Flop d_ff_44 (.D(Data_input[5]), .clk(and_12_out), .Q(d_ff_44_q));  // open: Qn, preset, reset
  D_Flip_Flop d_ff_45 (.D(Data_input[5]), .clk(and_13_out), .Q(d_ff_45_q));  // open: Qn, preset, reset
  D_Flip_Flop d_ff_46 (.D(Data_input[5]), .clk(and_14_out), .Q(d_ff_46_q));  // open: Qn, preset, reset
  D_Flip_Flop d_ff_47 (.D(Data_input[5]), .clk(and_15_out), .Q(d_ff_47_q));  // open: Qn, preset, reset
  D_Flip_Flop d_ff_48 (.D(Data_input[5]), .clk(and_16_out), .Q(d_ff_48_q));  // open: Qn, preset, reset
  and and_59 (and_59_out, and_8_out, d_ff_48_q);
  and and_60 (and_60_out, and_4_out, d_ff_44_q);
  and and_61 (and_61_out, and_5_out, d_ff_45_q);
  and and_62 (and_62_out, and_6_out, d_ff_46_q);
  and and_63 (and_63_out, and_7_out, d_ff_47_q);
  or or_6 (or_6_out, and_59_out, and_63_out, and_62_out, and_61_out, and_60_out, and_66_out, and_65_out, and_64_out);
  and and_64 (and_64_out, and_1_out, d_ff_41_q);
  and and_65 (and_65_out, and_2_out, d_ff_42_q);
  and and_66 (and_66_out, and_3_out, d_ff_43_q);
  assign Data_output[5] = and_18_out ? or_6_out : 1'bz;  // Controlled_Buffer controlled_buffer_6
  D_Flip_Flop d_ff_49 (.D(Data_input[6]), .clk(and_9_out), .Q(d_ff_49_q));  // open: Qn, preset, reset
  D_Flip_Flop d_ff_50 (.D(Data_input[6]), .clk(and_10_out), .Q(d_ff_50_q));  // open: Qn, preset, reset
  D_Flip_Flop d_ff_51 (.D(Data_input[6]), .clk(and_11_out), .Q(d_ff_51_q));  // open: Qn, preset, reset
  D_Flip_Flop d_ff_52 (.D(Data_input[6]), .clk(and_12_out), .Q(d_ff_52_q));  // open: Qn, preset, reset
  D_Flip_Flop d_ff_53 (.D(Data_input[6]), .clk(and_13_out), .Q(d_ff_53_q));  // open: Qn, preset, reset
  D_Flip_Flop d_ff_54 (.D(Data_input[6]), .clk(and_14_out), .Q(d_ff_54_q));  // open: Qn, preset, reset
  D_Flip_Flop d_ff_55 (.D(Data_input[6]), .clk(and_15_out), .Q(d_ff_55_q));  // open: Qn, preset, reset
  D_Flip_Flop d_ff_56 (.D(Data_input[6]), .clk(and_16_out), .Q(d_ff_56_q));  // open: Qn, preset, reset
  and and_67 (and_67_out, and_6_out, d_ff_54_q);
  and and_68 (and_68_out, and_7_out, d_ff_55_q);
  and and_69 (and_69_out, and_8_out, d_ff_56_q);
  and and_70 (and_70_out, and_2_out, d_ff_50_q);
  and and_71 (and_71_out, and_3_out, d_ff_51_q);
  and and_72 (and_72_out, and_4_out, d_ff_52_q);
  and and_73 (and_73_out, and_5_out, d_ff_53_q);
  or or_7 (or_7_out, and_69_out, and_68_out, and_67_out, and_73_out, and_72_out, and_71_out, and_70_out, and_74_out);
  D_Flip_Flop d_ff_57 (.D(Data_input[7]), .clk(and_9_out), .Q(d_ff_57_q));  // open: Qn, preset, reset
  and and_74 (and_74_out, and_1_out, d_ff_49_q);
  D_Flip_Flop d_ff_58 (.D(Data_input[7]), .clk(and_10_out), .Q(d_ff_58_q));  // open: Qn, preset, reset
  D_Flip_Flop d_ff_59 (.D(Data_input[7]), .clk(and_11_out), .Q(d_ff_59_q));  // open: Qn, preset, reset
  D_Flip_Flop d_ff_60 (.D(Data_input[7]), .clk(and_12_out), .Q(d_ff_60_q));  // open: Qn, preset, reset
  D_Flip_Flop d_ff_61 (.D(Data_input[7]), .clk(and_13_out), .Q(d_ff_61_q));  // open: Qn, preset, reset
  D_Flip_Flop d_ff_62 (.D(Data_input[7]), .clk(and_14_out), .Q(d_ff_62_q));  // open: Qn, preset, reset
  D_Flip_Flop d_ff_63 (.D(Data_input[7]), .clk(and_15_out), .Q(d_ff_63_q));  // open: Qn, preset, reset
  D_Flip_Flop d_ff_64 (.D(Data_input[7]), .clk(and_16_out), .Q(d_ff_64_q));  // open: Qn, preset, reset
  assign Data_output[6] = and_18_out ? or_7_out : 1'bz;  // Controlled_Buffer controlled_buffer_7
  and and_75 (and_75_out, and_7_out, d_ff_63_q);
  and and_76 (and_76_out, and_8_out, d_ff_64_q);
  and and_77 (and_77_out, and_3_out, d_ff_59_q);
  and and_78 (and_78_out, and_4_out, d_ff_60_q);
  and and_79 (and_79_out, and_5_out, d_ff_61_q);
  and and_80 (and_80_out, and_6_out, d_ff_62_q);
  or or_8 (or_8_out, and_76_out, and_75_out, and_80_out, and_79_out, and_78_out, and_77_out, and_82_out, and_81_out);
  and and_81 (and_81_out, and_1_out, d_ff_57_q);
  and and_82 (and_82_out, and_2_out, d_ff_58_q);
  assign Data_output[7] = and_18_out ? or_8_out : 1'bz;  // Controlled_Buffer controlled_buffer_8
endmodule

module with_keyboard (
);

  wire button_1_out, button_2_out, clock_1_out, not_1_out;
  wire [2:0] counter_1_q;
  wire [6:0] bitselector_1_out;
  wire [7:0] ram_1_dout, undriven;

  Counter #(.max('h7), .width(3)) counter_1 (
    .Q(counter_1_q), .clk(clock_1_out), .clr(button_1_out));  // open: load, D, count, carry, up
  Button button_1 (.out(button_1_out));
  Clock clock_1 (.out(clock_1_out));
  Random random_1 ();  // open: clk, next, out, clr
  not not_1 (not_1_out, clock_1_out);
  RAM #(.addrWidth(3)) ram_1 (
    .addr(counter_1_q), .we(clock_1_out), .oe(not_1_out), .clk(clock_1_out), .din(undriven), .dout(ram_1_dout));
  BitSelector #(.group(7)) bitselector_1 (.in(ram_1_dout), .out(bitselector_1_out), .sel(clock_1_out));
  TTY #(.rows(16)) tty_1 (.data(bitselector_1_out), .clk(clock_1_out), .we(1'b1), .clr(button_2_out));
  Button button_2 (.out(button_2_out));
endmodule
